// Logisim project processador.circ as structural Verilog
module Add_1 (
  input  a,
  input  b,
  input  Vem_1,
  output S,
  output Vai_1
);

  wire and_1_out, and_2_out, or_1_out, xor_1_out;

  xor xor_1 (xor_1_out, b, a);
  or or_1 (or_1_out, Vem_1, b);
  and and_1 (and_1_out, b, Vem_1);
  xor xor_2 (S, Vem_1, xor_1_out);
  and and_2 (and_2_out, or_1_out, a);
  or or_2 (Vai_1, and_2_out, and_1_out);
endmodule

module Somador_4bits (
  input  [3:0] B,
  input  [3:0] A,
  output Of,
  output [3:0] Soma
);

  wire add_1_2_vai_1, add_1_3_vai_1, add_1_4_vai_1;

  // Probe on A
  Add_1 add_1_1 (.S(Soma[3]), .Vai_1(Of), .a(A[3]), .b(B[3]), .Vem_1(add_1_2_vai_1));
  Add_1 add_1_2 (.S(Soma[2]), .Vai_1(add_1_2_vai_1), .a(A[2]), .b(B[2]), .Vem_1(add_1_3_vai_1));
  Add_1 add_1_3 (.S(Soma[1]), .Vai_1(add_1_3_vai_1), .a(A[1]), .b(B[1]), .Vem_1(add_1_4_vai_1));
  // Probe on Soma
  Add_1 add_1_4 (.S(Soma[0]), .Vai_1(add_1_4_vai_1), .a(A[0]), .b(B[0]), .Vem_1(1'b0));
  // Probe on B
endmodule

module Sub_1 (
  input  a,
  input  b,
  input  Vem_1,
  output S,
  output Vai_1
);

  wire and_1_out, and_2_out, or_1_out, xor_1_out;

  xor xor_1 (xor_1_out, b, a);
  or or_1 (or_1_out, Vem_1, b);
  and and_1 (and_1_out, b, Vem_1);
  xor xor_2 (S, Vem_1, xor_1_out);
  and and_2 (and_2_out, or_1_out, ~a);  // AND_Gate
  or or_2 (Vai_1, and_2_out, and_1_out);
endmodule

module Subtrator_4bits (
  input  [3:0] B,
  input  [3:0] A,
  input  in_3,
  output Overflow,
  output [3:0] Soma
);

  wire sub_1_2_vai_1, sub_1_3_vai_1, sub_1_4_vai_1;

  // Probe on A
  Sub_1 sub_1_1 (.S(Soma[3]), .Vai_1(Overflow), .a(A[3]), .b(B[3]), .Vem_1(sub_1_2_vai_1));
  Sub_1 sub_1_2 (.S(Soma[2]), .Vai_1(sub_1_2_vai_1), .a(A[2]), .b(B[2]), .Vem_1(sub_1_3_vai_1));
  Sub_1 sub_1_3 (.S(Soma[1]), .Vai_1(sub_1_3_vai_1), .a(A[1]), .b(B[1]), .Vem_1(sub_1_4_vai_1));
  // Probe on Soma
  Sub_1 sub_1_4 (.S(Soma[0]), .Vai_1(sub_1_4_vai_1), .a(A[0]), .b(B[0]), .Vem_1(in_3));
  // Probe on B
endmodule

module Buf (
  input  [3:0] A,
  input  Controle,
  output [3:0] S
);

  assign S[3] = Controle ? A[3] : 1'bz;  // Controlled_Buffer controlled_buffer_1
  assign S[1] = Controle ? A[1] : 1'bz;  // Controlled_Buffer controlled_buffer_2
  assign S[0] = Controle ? A[0] : 1'bz;  // Controlled_Buffer controlled_buffer_3
  assign S[2] = Controle ? A[2] : 1'bz;  // Controlled_Buffer controlled_buffer_4
endmodule

module Decod (
  input  [2:0] \Operação ,
  output s0,
  output s1,
  output s2,
  output s3,
  output s4,
  output s5,
  output s6,
  output s7
);

  wire not_1_out, not_2_out, not_3_out, not_4_out, not_5_out, not_6_out, not_7_out, not_8_out, not_9_out,
       not_10_out, not_11_out, not_12_out;

  not not_1 (not_1_out, \Operação [2]);
  not not_2 (not_2_out, \Operação [1]);
  not not_3 (not_3_out, \Operação [0]);
  not not_4 (not_4_out, \Operação [2]);
  not not_5 (not_5_out, \Operação [1]);
  not not_6 (not_6_out, \Operação [2]);
  not not_7 (not_7_out, \Operação [0]);
  not not_8 (not_8_out, \Operação [2]);
  not not_9 (not_9_out, \Operação [1]);
  not not_10 (not_10_out, \Operação [0]);
  not not_11 (not_11_out, \Operação [1]);
  not not_12 (not_12_out, \Operação [0]);
  and and_1 (s7, \Operação [2], \Operação [1], \Operação [0]);
  and and_2 (s0, not_1_out, not_2_out, not_3_out);
  and and_3 (s1, not_4_out, not_5_out, \Operação [0]);
  and and_4 (s2, not_6_out, \Operação [1], not_7_out);
  and and_5 (s3, not_8_out, \Operação [1], \Operação [0]);
  and and_6 (s4, \Operação [2], not_9_out, not_10_out);
  and and_7 (s5, \Operação [2], not_11_out, \Operação [0]);
  and and_8 (s6, \Operação [2], \Operação [1], not_12_out);
endmodule

module Right (
  input  [3:0] ABCD,
  input  [1:0] XY,
  output [3:0] abcd_2
);

  wire and_1_out, and_2_out, and_3_out, and_4_out, and_5_out, and_6_out, and_7_out, and_8_out, and_9_out;

  and and_1 (and_1_out, ~XY[1], ~XY[0], ABCD[0]);  // AND_Gate
  and and_2 (and_2_out, ~XY[1], XY[0], ABCD[1]);  // AND_Gate
  and and_3 (and_3_out, XY[1], ~XY[0], ABCD[2]);  // AND_Gate
  and and_4 (and_4_out, XY[1], XY[0], ABCD[3]);
  and and_5 (and_5_out, ~XY[1], ~XY[0], ABCD[1]);  // AND_Gate
  and and_6 (and_6_out, ~XY[1], XY[0], ABCD[2]);  // AND_Gate
  and and_7 (and_7_out, XY[1], ~XY[0], ABCD[3]);  // AND_Gate
  and and_8 (and_8_out, ~XY[1], ~XY[0], ABCD[2]);  // AND_Gate
  and and_9 (and_9_out, ~XY[1], XY[0], ABCD[3]);  // AND_Gate
  and and_10 (abcd_2[3], ~XY[1], ~XY[0], ABCD[3]);  // AND_Gate
  or or_1 (abcd_2[0], and_1_out, and_2_out, and_3_out, and_4_out);
  or or_2 (abcd_2[1], and_5_out, and_6_out, and_7_out);
  or or_3 (abcd_2[2], and_8_out, and_9_out);
endmodule

module Left (
  input  [3:0] ABCD,
  input  [1:0] XY,
  output [3:0] abcd_2
);

  wire and_1_out, and_2_out, and_3_out, and_4_out, and_5_out, and_6_out, and_7_out, and_8_out, and_9_out;

  and and_1 (and_1_out, ~XY[1], ~XY[0], ABCD[3]);  // AND_Gate
  and and_2 (and_2_out, ~XY[1], XY[0], ABCD[2]);  // AND_Gate
  and and_3 (and_3_out, XY[1], ~XY[0], ABCD[1]);  // AND_Gate
  and and_4 (and_4_out, XY[1], XY[0], ABCD[0]);
  and and_5 (and_5_out, ~XY[1], ~XY[0], ABCD[2]);  // AND_Gate
  and and_6 (and_6_out, ~XY[1], XY[0], ABCD[1]);  // AND_Gate
  and and_7 (and_7_out, XY[1], ~XY[0], ABCD[0]);  // AND_Gate
  and and_8 (and_8_out, ~XY[1], ~XY[0], ABCD[1]);  // AND_Gate
  and and_9 (and_9_out, ~XY[1], XY[0], ABCD[0]);  // AND_Gate
  and and_10 (abcd_2[0], ~XY[1], ~XY[0], ABCD[0]);  // AND_Gate
  or or_1 (abcd_2[3], and_1_out, and_2_out, and_3_out, and_4_out);
  or or_2 (abcd_2[2], and_5_out, and_6_out, and_7_out);
  or or_3 (abcd_2[1], and_8_out, and_9_out);
endmodule

module Or_4bits (
  input  [3:0] B,
  input  [3:0] A,
  output [3:0] S
);

  or or_1 (S[2], A[2], B[2]);
  or or_2 (S[3], A[3], B[3]);
  or or_3 (S[1], A[1], B[1]);
  or or_4 (S[0], A[0], B[0]);
endmodule

module Not_4bits (
  input  [3:0] B,
  output [3:0] S
);

  not not_1 (S[0], B[0]);
  not not_2 (S[1], B[1]);
  not not_3 (S[2], B[2]);
  not not_4 (S[3], B[3]);
endmodule

module ULA (
  input  D,
  input  [3:0] A,
  input  [3:0] B,
  input  [2:0] in_4
);

  wire decod_1_s0, decod_1_s1, decod_1_s2, decod_1_s3, decod_1_s4, decod_1_s5, not_1_out;
  wire [3:0] buf_7_s, left_1_abcd_2, not_4bits_1_s, or_4bits_1_s, right_1_abcd_2, somador_4bits_1_soma,
       subtrator_4bits_1_soma;

  Buf buf_1 (.A(B), .Controle(decod_1_s0));  // open: S
  Decod decod_1 (
    .\Operação (in_4), .s0(decod_1_s0), .s1(decod_1_s1), .s2(decod_1_s2), .s3(decod_1_s3), .s4(decod_1_s4),
    .s5(decod_1_s5));  // open: s6, s7
  Somador_4bits somador_4bits_1 (.B(A), .A(B), .Soma(somador_4bits_1_soma));  // open: Of
  Buf buf_2 (.A(somador_4bits_1_soma), .Controle(decod_1_s1));  // open: S
  Buf buf_3 (.A(subtrator_4bits_1_soma), .Controle(decod_1_s2));  // open: S
  Subtrator_4bits subtrator_4bits_1 (.B(B), .A(A), .Soma(subtrator_4bits_1_soma));  // open: Overflow, in_3
  Buf buf_4 (.A(or_4bits_1_s), .Controle(decod_1_s3));  // open: S
  Buf buf_5 (.A(not_4bits_1_s), .Controle(decod_1_s4));  // open: S
  Or_4bits or_4bits_1 (.A(A), .B(B), .S(or_4bits_1_s));
  Buf buf_6 (.A(buf_7_s), .Controle(decod_1_s5));  // open: S
  Not_4bits not_4bits_1 (.B(B), .S(not_4bits_1_s));
  Left left_1 (.ABCD(A), .XY(B[1:0]), .abcd_2(left_1_abcd_2));
  Right right_1 (.ABCD(A), .XY(B[1:0]), .abcd_2(right_1_abcd_2));
  not not_1 (not_1_out, D);
  Buf buf_7 (.A(left_1_abcd_2), .Controle(not_1_out), .S(buf_7_s));
  Buf buf_8 (.A(right_1_abcd_2), .Controle(D), .S(buf_7_s));
endmodule
